# Fritzing sketch design (saved by Fritzing 1.0.6)
circuit board: 2.68327cm x 6.4091cm
perfboards: 1

parts:
  A1 = ESP32 38Pin narrow
  DHT1 = DHT11 Humitidy and Temperature Sensor (3 pins)
  R1 = Resistor [tolerance=±5% power=0.25W resistance=4.7k package=THT]

nets:
  N1: A1.Pin_1, DHT1.Plus, R1.Pin_1
  N2: A1.Pin_11, DHT1.Signal, R1.Pin_0
  N3: A1.Pin_14, A1.Pin_32, A1.Pin_38, DHT1.Gnd

custom parts:
  ESP32 38Pin narrow: ESP32 38Pin narrow.
  DHT11 Humitidy and Temperature Sensor (3 pins): DHT11 Humidity and Temperature Sensor (3 pins).
